# Fritzing sketch Boxes (saved by Fritzing 0.9.3b)
breadboards: 1

parts:
  Part1 = Arduino Due (Rev2b)
  Part2 = ws2812b [package="smd 2812b"]
  IC1 = ULN2803A [package=THT]
  IC2 = ULN2803A [package=THT]
  IC3 = ULN2803A [package=THT]
  D1 = Rectifier Diode [part_number=1N4001 package="300 mil [THT]"]
  D2 = Rectifier Diode [part_number=1N4001 package="300 mil [THT]"]  # not connected
  D3 = Rectifier Diode [part_number=1N4001 package="300 mil [THT]"]  # not connected
  D4 = Rectifier Diode [part_number=1N4001 package="300 mil [THT]"]  # not connected
  D5 = Rectifier Diode [part_number=1N4001 package="300 mil [THT]"]  # not connected
  D6 = Rectifier Diode [part_number=1N4001 package="300 mil [THT]"]  # not connected
  D7 = Rectifier Diode [part_number=1N4001 package="300 mil [THT]"]  # not connected
  D8 = Rectifier Diode [part_number=1N4001 package="300 mil [THT]"]
  U1 = MAX485 [package=dil08]
  J1 = Dagu DGServo 9g header (male) [package=THT]
  J2 = Dagu DGServo 9g header (male) [package=THT]
  Power_plug1 = Power plug
  Power_plug2 = Power plug
  S1 = Round Pushbutton
  S_LED1 = smd LED [color="Red (633nm)" package="0805 [SMD]"]
  UFO1 = LTE-302 [package=lte-302]
  S2 = Round Pushbutton
  S_LED2 = smd LED [color="Red (633nm)" package="0805 [SMD]"]
  UFO2 = LTE-302 [package=lte-302]
  L1 = Solenoid
  L2 = Solenoid

nets:
  N1: Part1.D18/TX1, U1.RO
  N2: Part1.D19/RX1, U1.DI
  N3: Part1.D20/SDA3, U1.RE, U1.DE
  N4: Part1.VIN, IC1.COM_-_Common, IC2.COM_-_Common, IC3.COM_-_Common
  N5: Part1.D12_PWM, Part2.DIN
  5V: Part1.5V, U1.VCC
  N6: Part1.D22, IC3.In_1
  N7: Part1.D23, IC1.In_1
  N8: Part1.D36, IC3.In_8
  N9: Part1.D37, IC1.In_8
  N10: Part1.D38, D1.anode
  N11: Part1.D39, IC2.In_1
  N12: Part1.D52, D8.anode
  N13: Part1.D53, IC2.In_8
  GND: Part1.GND, IC1.0V, IC2.0V, IC3.0V, U1.GND, J1.gnd, J2.gnd
  VDD: Part2.VDD, Power_plug1.VCC
  VSS: Part2.VSS, Power_plug1.GND
  N14: IC1.Out_8, S_LED2.cathode
  N15: IC1.Out_1, S_LED1.cathode
  N16: IC2.Out_8, UFO2.C
  N17: IC2.Out_1, UFO1.C
  N18: IC3.Out_8, L2.pin1
  N19: IC3.Out_1, L1.pin1
  N20: D1.cathode, S1.leg0
  N21: D8.cathode, S2.leg0
  VCC: U1.A, J1.Vcc, J2.Vcc
  N22: U1.B, J1.pulse, J2.pulse
  N23: Power_plug2.GND, S1.leg1, S2.leg1
  N24: Power_plug2.VCC, S_LED1.anode, UFO1.A, S_LED2.anode, UFO2.A, L1.pin2, L2.pin2

notes:
  5V
  12V
  BOX1
  BOX2-8
  LED RIBBON
  MODBUS
  UFO1
